// Digital circuit assembler.dig as structural Verilog
module assembler (
  input  prog,
  input  [15:0] Value,
  input  [3:0] Dest,
  input  [3:0] Src,
  input  srcEn,
  input  add,
  input  sub,
  input  mul,
  input  div,
  input  \and ,
  input  \or ,
  input  eq,
  input  greater,
  input  smaller,
  input  mov,
  input  mod,
  input  sw,
  input  lw,
  input  jumpT,
  input  jumtF,
  input  jump,
  input  [22:0] mem_adrs,
  output [31:0] \output ,
  output strClk
);

  wire priorityencoder_1_any, priorityencoder_2_any;

  PriorityEncoder #(.Selector_Bits(4)) priorityencoder_1 (
    .in0(add), .in1(sub), .in2(mul), .in3(div), .in4(\and ), .in5(\or ), .in6(eq), .in7(greater),
    .in8(smaller), .in9(mov), .in10(mod), .in11(sw), .in12(lw), .in13(jumpT), .in14(jumtF), .in15(jump),
    .num(\output [30:27]), .any(priorityencoder_1_any));
  PriorityEncoder #(.Selector_Bits(3)) priorityencoder_2 (
    .in0(sw), .in1(lw), .in2(jumpT), .in3(jumtF), .in4(jump), .in5(1'b0), .in6(1'b0), .in7(1'b0),
    .any(priorityencoder_2_any));  // open: num
  Multiplexer #(.Bits(16)) multiplexer_1 (
    .sel(priorityencoder_2_any), .in_0(Value), .in_1(mem_adrs[15:0]), .out(\output [15:0]));
  Multiplexer #(.Bits(3)) multiplexer_2 (
    .sel(priorityencoder_2_any), .in_0(3'b000), .in_1(mem_adrs[18:16]), .out(\output [18:16]));
  and and_1 (strClk, priorityencoder_1_any, prog);
  Multiplexer #(.Bits(4)) multiplexer_3 (
    .sel(priorityencoder_2_any), .in_0(Src), .in_1(mem_adrs[22:19]), .out(\output [22:19]));

  assign {\output [31], \output [26:23]} = {srcEn, Dest};

  // Notes on the sheet:
  //   Arithmetic operations
  //   Memory operations
endmodule
