// Digital circuit decoder.dig as structural Verilog
module decoder (
  input  [31:0] inst,
  output [3:0] dest,
  output [3:0] src,
  output [3:0] Opr,
  output [15:0] Value,
  output srcEn,
  output [22:0] Mem_adres
);


  assign dest = inst[26:23];
  assign Mem_adres = inst[22:0];
  assign Opr = inst[30:27];
  assign src = inst[22:19];
  assign srcEn = inst[31];
  assign Value = inst[15:0];
endmodule
