// Digital circuit execute.dig as structural Verilog
module execute (
  input  [15:0] rA,
  input  [15:0] rB,
  input  [3:0] opr,
  input  [15:0] A,
  input  srcEn,
  output [15:0] \output ,
  output move_en,
  output LW_en,
  output SW_en,
  output jump_en,
  output cf
);

  wire and_2_out, and_3_out, and_4_out, and_5_out, and_6_out, comparator_1_eq, comparator_1_gt,
       comparator_1_lt, decoder_1_out_0, decoder_1_out_1, decoder_1_out_2, decoder_1_out_3, decoder_1_out_4,
       decoder_1_out_5, decoder_1_out_6, decoder_1_out_7, decoder_1_out_8, decoder_1_out_9, decoder_1_out_10,
       decoder_1_out_13, decoder_1_out_14, decoder_1_out_15, not_1_out, or_2_out, or_4_out;
  wire [15:0] add_1_s, and_1_out, div_1_q, div_1_r, multiplexer_1_out, or_1_out, sub_1_s;
  wire [31:0] mul_1_mul;

  Multiplexer #(.Bits(16)) multiplexer_1 (.sel(srcEn), .in_0(A), .in_1(rA), .out(multiplexer_1_out));
  Add #(.Bits(16)) add_1 (.a(multiplexer_1_out), .b(rB), .c_i(1'b0), .s(add_1_s));  // open: c_o
  Sub #(.Bits(16)) sub_1 (.a(multiplexer_1_out), .b(rB), .c_i(1'b0), .s(sub_1_s));  // open: c_o
  Mul #(.Bits(16)) mul_1 (.a(multiplexer_1_out), .b(rB), .mul(mul_1_mul));
  Div #(.Bits(16)) div_1 (.a(multiplexer_1_out), .b(rB), .q(div_1_q), .r(div_1_r));
  assign and_1_out = multiplexer_1_out & rB;  // And and_1, 16 bits wide
  assign or_1_out = multiplexer_1_out | rB;  // Or or_1, 16 bits wide
  Comparator #(.Bits(16)) comparator_1 (
    .a(multiplexer_1_out), .b(rB), .gt(comparator_1_gt), .eq(comparator_1_eq), .lt(comparator_1_lt));
  Multiplexer #(.Selector_Bits(4), .Bits(16)) multiplexer_2 (
    .sel(opr), .in_0(add_1_s), .in_1(sub_1_s), .in_2(mul_1_mul[15:0]), .in_3(div_1_q), .in_4(and_1_out),
    .in_5(or_1_out), .in_6({16{1'b0}}), .in_7({16{1'b0}}), .in_8({16{1'b0}}), .in_9(multiplexer_1_out),
    .in_10(div_1_r), .in_11({16{1'b0}}), .in_12({16{1'b0}}), .in_13({16{1'b0}}), .in_14({16{1'b0}}),
    .in_15({16{1'b0}}), .out(\output ));
  Decoder #(.Selector_Bits(4)) decoder_1 (
    .sel(opr), .out_0(decoder_1_out_0), .out_1(decoder_1_out_1), .out_2(decoder_1_out_2),
    .out_3(decoder_1_out_3), .out_4(decoder_1_out_4), .out_5(decoder_1_out_5), .out_6(decoder_1_out_6),
    .out_7(decoder_1_out_7), .out_8(decoder_1_out_8), .out_9(decoder_1_out_9), .out_10(decoder_1_out_10),
    .out_11(SW_en), .out_12(LW_en), .out_13(decoder_1_out_13), .out_14(decoder_1_out_14),
    .out_15(decoder_1_out_15));
  not not_1 (not_1_out, cf);
  and and_2 (and_2_out, decoder_1_out_6, comparator_1_eq);
  and and_3 (and_3_out, decoder_1_out_7, comparator_1_gt);
  and and_4 (and_4_out, decoder_1_out_8, comparator_1_lt);
  or or_2 (or_2_out, decoder_1_out_6, decoder_1_out_7, decoder_1_out_8);
  and and_5 (and_5_out, decoder_1_out_13, cf);
  and and_6 (and_6_out, decoder_1_out_14, not_1_out);
  or or_3 (move_en, decoder_1_out_0, decoder_1_out_1, decoder_1_out_2, decoder_1_out_3, decoder_1_out_4, decoder_1_out_5, decoder_1_out_9, decoder_1_out_10, LW_en);
  or or_4 (or_4_out, and_2_out, and_3_out, and_4_out);
  or or_5 (jump_en, and_5_out, decoder_1_out_15, and_6_out);
  D_FF d_ff_1 (.D(or_4_out), .C(or_2_out), .Q(cf));  // open: nQ
endmodule
