// Digital circuit main.dig as structural Verilog
module main (
  input  [15:0] value,
  input  [3:0] dest,
  input  [3:0] src,
  input  [22:0] mem_adres,
  output [15:0] storage_b,
  output [15:0] ram_a,
  output [15:0] ram_b,
  output [3:0] output_en,
  output flag
);

  wire add_out, and_out, assembler_1_strclk, clock_out, clock_reset_out, decoder_1_srcen, div_out,
       empty_data_out, eq_out, execute_1_jump_en, execute_1_lw_en, execute_1_move_en, execute_1_sw_en,
       greater_out, jump_out, jumpF_out, jumpT_out, lw_out, mod_out, mode_out, mov_out, mul_out,
       multiplexer_2_out, or_2_out, or_3_out, or_out, smaller_out, srcEn_out, sub_out, sw_out;
  wire [3:0] decoder_1_dest, decoder_1_opr, decoder_1_src;
  wire [15:0] decoder_1_value, execute_1_output, multiplexer_3_out, registerfile_2_da;
  wire [22:0] decoder_1_mem_adres;
  wire [31:0] assembler_1_output, eepromdualport_1_d, multiplexer_1_out;

  LED Programming (.in(mode_out));
  DipSwitch mode (.out(mode_out));
  DipSwitch srcEn (.out(srcEn_out));
  Button add (.out(add_out));
  Button sub (.out(sub_out));
  Button mul (.out(mul_out));
  Button div (.out(div_out));
  Button \and  (.out(and_out));
  Button \or  (.out(or_out));
  Button eq (.out(eq_out));
  Button greater (.out(greater_out));
  Button smaller (.out(smaller_out));
  Button mov (.out(mov_out));
  Button mod (.out(mod_out));
  Button sw (.out(sw_out));
  Button lw (.out(lw_out));
  Button jumpT (.out(jumpT_out));
  Button jumpF (.out(jumpF_out));
  Button jump (.out(jump_out));
  assembler assembler_1 (
    .prog(mode_out), .Value(value), .Dest(dest), .Src(src), .srcEn(srcEn_out), .add(add_out), .sub(sub_out),
    .mul(mul_out), .div(div_out), .\and (and_out), .\or (or_out), .eq(eq_out), .greater(greater_out),
    .smaller(smaller_out), .mov(mov_out), .mod(mod_out), .sw(sw_out), .lw(lw_out), .jumpT(jumpT_out),
    .jumtF(jumpF_out), .jump(jump_out), .mem_adrs(mem_adres), .\output (assembler_1_output),
    .strClk(assembler_1_strclk));
  Multiplexer #(.Bits(32)) multiplexer_1 (
    .sel(empty_data_out), .in_0(assembler_1_output), .in_1({32{1'b0}}), .out(multiplexer_1_out));
  Multiplexer multiplexer_2 (.sel(empty_data_out), .in_0(assembler_1_strclk), .in_1(1'b1), .out(multiplexer_2_out));
  CounterPreset #(.Bits(4)) counterpreset_1 (
    .en(1'b1), .C(or_2_out), .dir(1'b0), .in(decoder_1_dest), .ld(execute_1_jump_en), .clr(clock_reset_out),
    .out(output_en), .ovf(flag));
  EEPROMDualPort #(.AddrBits(4), .Bits(32)) eepromdualport_1 (
    .A(output_en), .Din(multiplexer_1_out), .str(1'b1), .C(multiplexer_2_out), .ld(1'b1),
    .D(eepromdualport_1_d));
  or or_2 (or_2_out, assembler_1_strclk, clock_out, clock_reset_out, empty_data_out);
  decoder decoder_1 (
    .inst(eepromdualport_1_d), .dest(decoder_1_dest), .src(decoder_1_src), .Opr(decoder_1_opr),
    .Value(decoder_1_value), .srcEn(decoder_1_srcen), .Mem_adres(decoder_1_mem_adres));
  Button empty_data (.out(empty_data_out));
  Button clock_reset (.out(clock_reset_out));
  Button clock (.out(clock_out));
  execute execute_1 (
    .rA(ram_a), .rB(ram_b), .opr(decoder_1_opr), .A(decoder_1_value), .srcEn(decoder_1_srcen),
    .\output (execute_1_output), .move_en(execute_1_move_en), .LW_en(execute_1_lw_en),
    .SW_en(execute_1_sw_en), .jump_en(execute_1_jump_en));  // open: cf
  Multiplexer #(.Bits(16)) multiplexer_3 (
    .sel(execute_1_lw_en), .in_0(execute_1_output), .in_1(registerfile_2_da), .out(multiplexer_3_out));
  or or_3 (or_3_out, execute_1_lw_en, execute_1_sw_en);
  RegisterFile #(.AddrBits(4), .Bits(16)) registerfile_1 (
    .Din(multiplexer_3_out), .we(execute_1_move_en), .Rw(decoder_1_dest), .C(clock_out), .Ra(decoder_1_src),
    .Rb(decoder_1_dest), .Da(ram_a), .Db(ram_b));
  RegisterFile #(.AddrBits(23), .Bits(16)) registerfile_2 (
    .Din(ram_a), .we(execute_1_sw_en), .Rw(decoder_1_mem_adres), .C(or_3_out), .Ra(decoder_1_mem_adres),
    .Rb(decoder_1_mem_adres), .Da(registerfile_2_da), .Db(storage_b));

  // Notes on the sheet:
  //   contents of eepromdualport_1 (hex, n*v repeats v):
  //   48000001,48800002,80800000,58000000,62000000
endmodule
